# Fritzing sketch circuit (saved by Fritzing 0.9.3b)
breadboards: 1

parts:
  Part1 = Arduino Nano (Rev3.0)
  Part2 = Matrix LED de 8x8 basada en MAX7219
  S1 = Momentary Switch [package=ksa_sealed_tac_switch]
  R1 = Resistor [tolerance=±5% resistance=220 package="2512 [SMD]"]

nets:
  GND: Part1.GND, Part2.GND, R1.Pin_1
  N1: Part1.D2, S1.1
  N2: Part1.D8, Part2.DIN
  N3: Part1.D9, Part2.CS
  N4: Part1.D10, Part2.CLK
  5V: Part1.5V, Part2.VCC, S1.4
